# Fritzing sketch espxx_weather_logger (saved by Fritzing 0.9.3b)

parts:
  U2 = NodeMCU V1.0
  J2 = male pin header, 3 pins [form="♂ (male)"]

nets:
  N1: U2.D0, U2.RST
  N2: U2.3V3, J2.pin2
  N3: U2.GND, J2.pin3
  N4: U2.D6, J2.pin1

notes:
  3.3 volts or above
  to Vin and GND
  Weather Logger to Thingspeak

custom parts:
  NodeMCU V1.0: ESP8266 based NodeMCU
